# Fritzing sketch esq (saved by Fritzing 0.9.2b)
breadboards: 1

parts:
  Componente1 = Arduino Mega 2560 (Rev3)
  kEYPAD_MATRICIAL_1 = KEYPAD 4x3

nets:
  N1: Componente1.D22, kEYPAD_MATRICIAL_1.col1
  N2: Componente1.D24, kEYPAD_MATRICIAL_1.arrow1
  N3: Componente1.D26, kEYPAD_MATRICIAL_1.col2
  N4: Componente1.D28, kEYPAD_MATRICIAL_1.arrow2
  N5: Componente1.D30, kEYPAD_MATRICIAL_1.col3
  N6: Componente1.D32, kEYPAD_MATRICIAL_1.arrow3
  N7: Componente1.D34, kEYPAD_MATRICIAL_1.arrow4

custom parts:
  KEYPAD 4x3: KEYPAD matricial de 12 botones, 4 filas x 3 columnas
