# Fritzing sketch esquema (saved by Fritzing 0.9.2b)
breadboards: 1

parts:
  Componente1 = Arduino Mega 2560 (Rev3)
  Componente2 = LCD Keypad Shield  # not connected
  Componente3 = Passive Buzzer
  kEYPAD_MATRICIAL_1 = KEYPAD 4x3
  R2 = Resistor [tolerance=±5% resistance=220 package=THT]
  LED1 = LED - 5mm [color="Red (633nm)" package="5 mm [THT]"]
  LED2 = LED - 5mm [color="Green (565nm)" package="5 mm [THT]"]
  R3 = Resistor [tolerance=±5% resistance=220 package=THT]

nets:
  N1: Componente1.D14/TX3, Componente3.S
  N2: Componente1.5V, Componente1.D49, Componente1.D50, Componente1.D51, Componente1.D52
  N3: Componente1.D22, kEYPAD_MATRICIAL_1.col1
  N4: Componente1.D24, kEYPAD_MATRICIAL_1.arrow1
  N5: Componente1.D26, kEYPAD_MATRICIAL_1.col2
  N6: Componente1.D28, kEYPAD_MATRICIAL_1.arrow2
  N7: Componente1.D30, kEYPAD_MATRICIAL_1.col3
  N8: Componente1.D31, R2.Pin_0
  N9: Componente1.D32, kEYPAD_MATRICIAL_1.arrow3
  N10: Componente1.D33, R3.Pin_0
  N11: Componente1.D34, kEYPAD_MATRICIAL_1.arrow4
  GND: Componente1.GND, Componente3.GND, LED1.anode, LED2.anode
  N12: R2.Pin_1, LED1.cathode
  N13: LED2.cathode, R3.Pin_1

custom parts:
  LCD Keypad Shield: It consists of a 1602 white character blue backlight LCD. The keypad consists of 5 keys — select, up, right, down and left. To save the digital IO pins, the keypad interface uses only one ADC channel. The key value is read through a 5 stage voltage divider.
  KEYPAD 4x3: KEYPAD matricial de 12 botones, 4 filas x 3 columnas
