# Fritzing sketch esquema (saved by Fritzing 0.9.2b)
breadboards: 1

parts:
  Componente1 = Arduino Mega 2560 (Rev3)
  Componente3 = Passive Buzzer
  kEYPAD_MATRICIAL_1 = KEYPAD 4x3
  R2 = Resistor [tolerance=±5% resistance=220 package=THT]
  LED1 = LED - 5mm [color="Red (633nm)" package="5 mm [THT]"]
  R3 = Resistor [tolerance=±5% resistance=220 package=THT]
  LED2 = LED - 5mm [color="Green (565nm)" package="5 mm [THT]"]
  LED3 = LED - 5mm [color="Red (633nm)" package="5 mm [THT]"]
  R4 = Resistor [tolerance=±5% resistance=220 package=THT]
  LCD1 = LCD screen  # not connected
  LCM1602_IIC2 = LCM1602 IIC [part_number="LCM1602 IIC" chip_label="LCM1602 IIC" package="DIP (Dual Inline) [THT]"]

nets:
  N1: Componente1.D21/SCL, LCM1602_IIC2.SCL
  N2: Componente1.D20/SDA, LCM1602_IIC2.SDA
  N3: Componente1.D14/TX3, Componente3.S
  GND: Componente1.GND, Componente3.GND, LED1.anode, LED2.anode, LED3.anode, LCM1602_IIC2.GND
  N4: Componente1.D10_PWM, R4.Pin_1
  5V: Componente1.5V, Componente1.D44, Componente1.D45, Componente1.D46, Componente1.D47, Componente1.D48, Componente1.D49, Componente1.D50, Componente1.D51, Componente1.D52, LCM1602_IIC2.VCC
  N5: Componente1.D22, kEYPAD_MATRICIAL_1.col1
  N6: Componente1.D24, kEYPAD_MATRICIAL_1.arrow1
  N7: Componente1.D26, kEYPAD_MATRICIAL_1.col2
  N8: Componente1.D28, kEYPAD_MATRICIAL_1.arrow2
  N9: Componente1.D30, kEYPAD_MATRICIAL_1.col3
  N10: Componente1.D32, kEYPAD_MATRICIAL_1.arrow3
  N11: Componente1.D34, kEYPAD_MATRICIAL_1.arrow4
  N12: Componente1.D35, R2.Pin_0
  N13: Componente1.D37, R3.Pin_0
  N14: R2.Pin_1, LED1.cathode
  N15: R3.Pin_1, LED2.cathode

notes:
  Este led pisca ao junto bom o beep do buzzer
  Esses leds piscam quando a bomba é ligada. Ficam alternando.
  Após a bomba ser iniciada eles irão piscar vermelho quando errar um código e verde quando acertar, além do sinal sonoro
  Aqui não é necessário seguir exatamente as mesmas cores nas mesmas posições, basta conectá-las todas à fonte 5v.
  Todos os fios devem ser de cor diferente, esses são os fios que deverão ser desconectados.
  Quando finalizado aqui, as variáveis no código devem ser atualizadas, ex:
  //fios
  const int fpreto = 53;
  const int fbranco = 51;
  const int fcinza = 49;
  const int froxo = 47;
  const int fazul = 45;
  const int fverde = 52;
  const int famarelo = 50;
  const int flaranja = 48;
  const int fvermelho = 46;
  const int fmarrom = 44;
  Módulo i2c

custom parts:
  KEYPAD 4x3: KEYPAD matricial de 12 botones, 4 filas x 3 columnas
  LCM1602 IIC: I2C-Module to use a 1602 or 2004 LCD on with the wire.h libory Serial LCD Modul
